// Logisim project parte1_memoria.circ as structural Verilog: 3 circuits, main circuit main
module main (
  input  [5:0] Endereco,
  input  [7:0] DataEscrita,
  input  CLOCK,
  input  Escrita,
  output [7:0] DadoLido
);

  wire and_1_out, and_2_out, and_3_out, and_4_out, CS_RAM, decodificador_1_cs_io, decodificador_1_cs_reg,
       decodificador_1_cs_rom, not_1_out, not_2_out, odd_parity_1_out, odd_parity_2_out, ram_2_dout,
       xor_1_out;
  wire [7:0] bancoderegistradores_1_dadolido, IO_dout, ram_1_dout, rom_1_data;

  LED led_1 (.in(decodificador_1_cs_rom));
  LED led_2 (.in(CS_RAM));
  Decodificador decodificador_1 (
    .A5(Endereco[5]), .A4(Endereco[4]), .CS_ROM(decodificador_1_cs_rom), .CS_RAM(CS_RAM),
    .CS_REG(decodificador_1_cs_reg), .CS_IO(decodificador_1_cs_io));
  LED led_3 (.in(decodificador_1_cs_reg));
  LED led_4 (.in(decodificador_1_cs_io));
  and and_1 (and_1_out, decodificador_1_cs_io, Escrita);
  RAM #(.addrWidth(4)) IO (
    .addr(Endereco[3:0]), .we(and_1_out), .oe(1'b1), .clk(CLOCK), .din(DataEscrita), .dout(IO_dout));
  and and_2 (and_2_out, decodificador_1_cs_reg, Escrita);
  BancoDeRegistradores bancoderegistradores_1 (
    .RegWrite(and_2_out), .Endereco(Endereco[3:0]), .DadoEscrita(DataEscrita), .Clock(CLOCK),
    .DadoLido(bancoderegistradores_1_dadolido));
  and and_3 (and_3_out, CS_RAM, Escrita);
  RAM #(.addrWidth(4)) ram_1 (
    .addr(Endereco[3:0]), .we(and_3_out), .oe(1'b1), .clk(CLOCK), .din(DataEscrita), .dout(ram_1_dout));
  ROM #(.addrWidth(4)) rom_1 (.addr(Endereco[3:0]), .data(rom_1_data));
  xor odd_parity_1 (odd_parity_1_out, ram_1_dout[0], ram_1_dout[1], ram_1_dout[2], ram_1_dout[3], ram_1_dout[4], ram_1_dout[5], ram_1_dout[6], ram_1_dout[7]);
  xor odd_parity_2 (odd_parity_2_out, DataEscrita[0], DataEscrita[1], DataEscrita[2], DataEscrita[3], DataEscrita[4], DataEscrita[5], DataEscrita[6], DataEscrita[7]);
  not not_1 (not_1_out, odd_parity_2_out);
  Multiplexer #(.select(2), .width(8)) multiplexer_1 (
    .in0(rom_1_data), .in1(ram_1_dout), .in2(bancoderegistradores_1_dadolido), .in3(IO_dout), .out(DadoLido),
    .sel(Endereco[5:4]));
  RAM #(.addrWidth(4), .dataWidth(1)) ram_2 (
    .addr(Endereco[3:0]), .we(and_3_out), .oe(1'b1), .clk(CLOCK), .din(not_1_out), .dout(ram_2_dout));
  not not_2 (not_2_out, odd_parity_1_out);
  xor xor_1 (xor_1_out, ram_2_dout, not_2_out);
  and and_4 (and_4_out, CS_RAM, xor_1_out);
  LED ErroParidade (.in(and_4_out));

  // Other names for the same wires on the sheet: A5A4[1:0] = Endereco[5:4]; WRT_ENBL = Escrita

  // Notes on the sheet:
  //   contents of rom_1 (hex, n*v repeats v):
  //   1 2 3 4 5 6 7 8
endmodule

module Decodificador (
  input  A5,
  input  A4,
  output CS_ROM,
  output CS_RAM,
  output CS_REG,
  output CS_IO
);

  wire not_1_out, not_2_out;

  not not_1 (not_1_out, A4);
  not not_2 (not_2_out, A5);
  and and_1 (CS_ROM, not_1_out, not_2_out);
  and and_2 (CS_RAM, A4, not_2_out);
  and and_3 (CS_REG, not_1_out, A5);
  and and_4 (CS_IO, A4, A5);
endmodule

module BancoDeRegistradores (
  input  RegWrite,
  input  [3:0] Endereco,
  input  [7:0] DadoEscrita,
  input  Clock,
  output [7:0] DadoLido
);

  wire and_1_out, and_2_out, and_3_out, and_4_out, and_5_out, and_6_out, and_7_out, and_8_out, and_9_out,
       and_10_out, and_11_out, and_12_out, and_13_out, and_14_out, and_15_out, and_16_out, decoder_1_out0,
       decoder_1_out1, decoder_1_out2, decoder_1_out3, decoder_1_out4, decoder_1_out5, decoder_1_out6,
       decoder_1_out7, decoder_1_out8, decoder_1_out9, decoder_1_out10, decoder_1_out11, decoder_1_out12,
       decoder_1_out13, decoder_1_out14, decoder_1_out15;
  wire [7:0] Reg_0_q, Reg_1_q, Reg_2_q, Reg_3_q, Reg_4_q, Reg_5_q, Reg_6_q, Reg_7_q, Reg_8_q, Reg_9_q,
       Reg_10_q, Reg_11_q, Reg_12_q, Reg_13_q, Reg_14_q, Reg_15_q;

  Decoder #(.select(4)) decoder_1 (
    .out0(decoder_1_out0), .out1(decoder_1_out1), .out2(decoder_1_out2), .out3(decoder_1_out3),
    .out4(decoder_1_out4), .out5(decoder_1_out5), .out6(decoder_1_out6), .out7(decoder_1_out7),
    .out8(decoder_1_out8), .out9(decoder_1_out9), .out10(decoder_1_out10), .out11(decoder_1_out11),
    .out12(decoder_1_out12), .out13(decoder_1_out13), .out14(decoder_1_out14), .out15(decoder_1_out15),
    .sel(Endereco), .en(1'b1));
  and and_1 (and_1_out, decoder_1_out3, RegWrite);
  and and_2 (and_2_out, decoder_1_out7, RegWrite);
  and and_3 (and_3_out, decoder_1_out11, RegWrite);
  and and_4 (and_4_out, decoder_1_out15, RegWrite);
  and and_5 (and_5_out, decoder_1_out2, RegWrite);
  and and_6 (and_6_out, decoder_1_out6, RegWrite);
  and and_7 (and_7_out, decoder_1_out10, RegWrite);
  and and_8 (and_8_out, decoder_1_out14, RegWrite);
  and and_9 (and_9_out, decoder_1_out1, RegWrite);
  and and_10 (and_10_out, decoder_1_out5, RegWrite);
  and and_11 (and_11_out, decoder_1_out9, RegWrite);
  and and_12 (and_12_out, decoder_1_out13, RegWrite);
  and and_13 (and_13_out, decoder_1_out0, RegWrite);
  and and_14 (and_14_out, decoder_1_out4, RegWrite);
  and and_15 (and_15_out, decoder_1_out8, RegWrite);
  and and_16 (and_16_out, decoder_1_out12, RegWrite);
  Register Reg_0 (.D(DadoEscrita), .en(and_13_out), .clk(Clock), .Q(Reg_0_q));  // open: clr
  Register Reg_4 (.D(DadoEscrita), .en(and_14_out), .clk(Clock), .Q(Reg_4_q));  // open: clr
  Register Reg_8 (.D(DadoEscrita), .en(and_15_out), .clk(Clock), .Q(Reg_8_q));  // open: clr
  Register Reg_12 (.D(DadoEscrita), .en(and_16_out), .clk(Clock), .Q(Reg_12_q));  // open: clr
  Register Reg_1 (.D(DadoEscrita), .en(and_9_out), .clk(Clock), .Q(Reg_1_q));  // open: clr
  Register Reg_5 (.D(DadoEscrita), .en(and_10_out), .clk(Clock), .Q(Reg_5_q));  // open: clr
  Register Reg_9 (.D(DadoEscrita), .en(and_11_out), .clk(Clock), .Q(Reg_9_q));  // open: clr
  Register Reg_13 (.D(DadoEscrita), .en(and_12_out), .clk(Clock), .Q(Reg_13_q));  // open: clr
  Register Reg_2 (.D(DadoEscrita), .en(and_5_out), .clk(Clock), .Q(Reg_2_q));  // open: clr
  Register Reg_6 (.D(DadoEscrita), .en(and_6_out), .clk(Clock), .Q(Reg_6_q));  // open: clr
  Register Reg_10 (.D(DadoEscrita), .en(and_7_out), .clk(Clock), .Q(Reg_10_q));  // open: clr
  Register Reg_14 (.D(DadoEscrita), .en(and_8_out), .clk(Clock), .Q(Reg_14_q));  // open: clr
  Register Reg_3 (.D(DadoEscrita), .en(and_1_out), .clk(Clock), .Q(Reg_3_q));  // open: clr
  Register Reg_7 (.D(DadoEscrita), .en(and_2_out), .clk(Clock), .Q(Reg_7_q));  // open: clr
  Register Reg_11 (.D(DadoEscrita), .en(and_3_out), .clk(Clock), .Q(Reg_11_q));  // open: clr
  Register Reg_15 (.D(DadoEscrita), .en(and_4_out), .clk(Clock), .Q(Reg_15_q));  // open: clr
  Multiplexer #(.select(4), .width(8)) multiplexer_1 (
    .in0(Reg_0_q), .in1(Reg_1_q), .in2(Reg_2_q), .in3(Reg_3_q), .in4(Reg_4_q), .in5(Reg_5_q), .in6(Reg_6_q),
    .in7(Reg_7_q), .in8(Reg_8_q), .in9(Reg_9_q), .in10(Reg_10_q), .in11(Reg_11_q), .in12(Reg_12_q),
    .in13(Reg_13_q), .in14(Reg_14_q), .in15(Reg_15_q), .out(DadoLido), .sel(Endereco));

  // Other names for the same wires on the sheet: clk = Clock; D_write[7:0] = DadoEscrita;
  //   Fim_endereco[3:0] = Endereco
endmodule
