// Logisim project Micropramada_vf.circ as structural Verilog: 1 circuit, main circuit parte2_microprogramada
module parte2_microprogramada (
  input  RESET,
  input  OP_BEQ,
  input  in_3,
  output PCWrite,
  output PCWriteCond,
  output PCSource,
  output MemRead,
  output IRWrite,
  output RegWrite,
  output ALUSrcA,
  output ALUSrcB1,
  output ALUSrcB0,
  output ALUOp1,
  output ALUOp0,
  output uPC_2,
  output uPC_1,
  output uPC_0
);

  wire AC0, AC1, C, CLK, D0, D0r, D1, D1r, D2, D2r, FT0, N1, N2, nAC0, nAC1, nBEQ, nC, nFT0, nFT1, nP0, nP1,
       nP2, nRST, nSQ0, nSQ1, SELDSP, SELINC, SQ0, SQ1, T1, T2, U1, U2, X1A, X1B, X2A, X2B;
  wire [2:0] adder_1_out, multiplexer_1_out, PROX;

  Clock u_CLK (.out(CLK));
  Hex_Digit_Display DISPLAY_uPC (.value({1'b0, uPC_2, uPC_1, uPC_0}));  // open: dp
  Register #(.width(3)) upc (.D(PROX), .en(1'b1), .clk(CLK), .Q({uPC_2, uPC_1, uPC_0}), .clr(RESET));
  Adder #(.width(3)) adder_1 (.a({uPC_2, uPC_1, uPC_0}), .b(3'b001), .out(adder_1_out), .cin(1'b0));  // open: cout
  not not_1 (nFT1, ALUSrcB1);
  not not_2 (nFT0, FT0);
  not not_3 (nAC1, AC1);
  not not_4 (nAC0, AC0);
  not not_5 (nSQ1, SQ1);
  not not_6 (nSQ0, SQ0);
  ROM #(.addrWidth(3)) rom_1 (.addr({uPC_2, uPC_1, uPC_0}), .data({ALUOp1, ALUOp0, ALUSrcB1, FT0, AC1, AC0, SQ1, SQ0}));
  Multiplexer #(.width(3)) multiplexer_1 (.in0(3'b010), .in1(3'b100), .out(multiplexer_1_out), .sel(OP_BEQ));
  not not_7 (nBEQ, OP_BEQ);
  not not_8 (nRST, RESET);
  not not_9 (nP0, uPC_0);
  not not_10 (nP1, uPC_1);
  not not_11 (nP2, uPC_2);
  and and_1 (PCSource, AC1, AC0);
  and and_2 (C, uPC_1, uPC_0);
  Multiplexer #(.select(2), .width(3)) multiplexer_2 (
    .in0(adder_1_out), .in1(3'b000), .in2(multiplexer_1_out), .in3(3'b000), .out(PROX), .sel({SQ1, SQ0}));
  and and_3 (ALUSrcB0, nFT1, nFT0);
  and and_4 (ALUSrcA, nFT1, FT0);
  and and_5 (IRWrite, nAC1, AC0);
  and and_6 (RegWrite, AC1, nAC0);
  and and_7 (SELINC, nSQ1, nSQ0);
  and and_8 (SELDSP, SQ1, nSQ0);
  not not_12 (nC, C);
  and and_9 (X1A, uPC_1, nP0);
  buf and_10 (X1B, nP1);  // AND_Gate
  and and_11 (X2B, nP2, C);
  and and_12 (X2A, uPC_2, nC);
  or or_1 (N1, X1A, X1B);
  and and_13 (D0r, SELINC, nP0);
  and and_14 (U1, SELDSP, nBEQ);
  and and_15 (U2, SELDSP, OP_BEQ);
  or or_2 (N2, X2A, X2B);
  and and_16 (T1, SELINC, D0r);
  and and_17 (D0, D0r, nRST);
  or or_3 (D1r, T1, U1);
  and and_18 (T2, SELINC, N2);
  or or_4 (D2r, T2, U2);
  and and_19 (D1, D1r, nRST);
  and and_20 (D2, D2r, nRST);

  assign MemRead = IRWrite;
  assign PCWrite = ALUSrcB0;
  assign PCWriteCond = PCSource;

  // Other names for the same wires on the sheet: P0 = uPC_0; P1 = uPC_1; P2 = uPC_2; FT1 = ALUSrcB1; UO0 = ALUOp0;
  //   UO1 = ALUOp1; MEMR = IRWrite; PCW = ALUSrcB0; PCWC = PCSource; REGW = RegWrite; SRCA = ALUSrcA; ZERO = in_3

  // Notes on the sheet:
  //   RESET: initial=0x1
  //   in_3: initial=0x1
  //   contents of rom_1 (hex, n*v repeats v):
  //   4 22 90 19 5d
endmodule
