// Logisim project parte2_cabeada.circ as structural Verilog: 1 circuit, main circuit main
module main (
  input  RESET,
  input  BEQ,
  output PCWrite,
  output PCWriteCond,
  output PCSource,
  output MemRead,
  output IRWrite,
  output RegWrite,
  output ALUSrcA,
  output ALUSrcB1,
  output ALUSrcB0,
  output ALUOp1,
  output ALUOp0
);

  wire a, b, CLK, D0, D1, D2, nBEQ, nQ0, nQ1, nQ2;

  Clock u_CLK (.out(CLK));
  D_Flip_Flop FF2 (.D(D2), .clk(CLK), .Q(ALUOp0), .reset(RESET));  // open: Qn, preset
  D_Flip_Flop FF1 (.D(D1), .clk(CLK), .Q(ALUOp1), .reset(RESET));  // open: Qn, preset
  D_Flip_Flop FF0 (.D(D0), .clk(CLK), .Q(ALUSrcB1), .reset(RESET));  // open: Qn, preset
  not not_1 (nQ2, ALUOp0);
  not not_2 (nQ1, ALUOp1);
  not not_3 (nQ0, ALUSrcB1);
  not not_4 (nBEQ, BEQ);
  and and_1 (D2, nQ1, ALUSrcB1, BEQ);
  and and_2 (a, ALUOp1, nQ0);
  and and_3 (b, nQ1, ALUSrcB1, nBEQ);
  or or_1 (D1, a, b);
  and and_4 (D0, nQ2, nQ0);
  and and_5 (ALUSrcB0, nQ2, nQ1, nQ0);
  and and_6 (RegWrite, ALUOp1, ALUSrcB1);
  or or_2 (ALUSrcA, ALUOp0, ALUOp1);
  Hex_Digit_Display hex_digit_display_1 (.value({1'b0, ALUOp0, ALUOp1, ALUSrcB1}));  // open: dp

  assign IRWrite = ALUSrcB0;
  assign MemRead = ALUSrcB0;
  assign PCSource = ALUOp0;
  assign PCWrite = ALUSrcB0;
  assign PCWriteCond = ALUOp0;

  // Other names for the same wires on the sheet: Q0 = ALUSrcB1; Q1 = ALUOp1; Q2 = ALUOp0; S0 = ALUSrcB0
endmodule
